# Fritzing sketch MoisturePiezoSpeakerProMini9V (saved by Fritzing 0.9.2b)

parts:
  Piezo_Speaker = Piezo Speaker
  Part1 = Arduino Pro Mini v13
  part = Battery block 9V
  PART1 = SparkFun Soil Moisture Sensor [part_number=SEN-13322]
  BC337 = TRANSISTOR_NPN_2 [package=to-92]
  part_2 = Resistor [tolerance=±5% resistance=1k package="1206 [SMD]"]
  D2 = Rectifier Diode [package="Melf DO-213 AA [SMD]"]

nets:
  N1: Piezo_Speaker.pin1, BC337.C, D2.anode
  VCC: Piezo_Speaker.pin2, Part1.VCC, PART1.VCC, D2.cathode
  GND: Part1.GND, part.-, PART1.GND, BC337.E
  N2: Part1.RAW, part.+
  N3: Part1.A0, PART1.SIG
  N4: Part1.D3_PWM, part_2.Pin_1
  N5: BC337.B, part_2.Pin_0

custom parts:
  SparkFun Soil Moisture Sensor: The SparkFun Soil Moisture Sensor is a simple breakout for measuring the moisture in soil and similar materials.
